// Logisim project CRC.circ as structural Verilog: 2 circuits, main circuit CRC
module CRC (
  input  [7:0] A,
  input  [3:0] B,
  output [10:0] out_3
);

  wire [2:0] crc_4_1_r, crc_4_2_r, crc_4_3_r, crc_4_4_r, crc_4_5_r, crc_4_6_r;
  wire [3:1] crc_4_7_r;

  // Probe on A[7:4]
  CRC_4 crc_4_1 (.S1(A[7:4]), .S2(B), .r(crc_4_1_r));  // open: out_4
  CRC_4 crc_4_2 (.S1({crc_4_1_r, A[3]}), .S2(B), .r(crc_4_2_r));  // open: out_4
  CRC_4 crc_4_3 (.S1({crc_4_2_r, A[2]}), .S2(B), .r(crc_4_3_r));  // open: out_4
  CRC_4 crc_4_4 (.S1({crc_4_3_r, A[1]}), .S2(B), .r(crc_4_4_r));  // open: out_4
  CRC_4 crc_4_5 (.S1({crc_4_4_r, A[0]}), .S2(B), .r(crc_4_5_r));  // open: out_4
  CRC_4 crc_4_6 (.S1({crc_4_5_r, 1'b0}), .S2(B), .r(crc_4_6_r));  // open: out_4
  CRC_4 crc_4_7 (.S1({crc_4_6_r, 1'b0}), .S2(B), .r(crc_4_7_r));  // open: out_4
  CRC_4 crc_4_8 (.S1({crc_4_7_r, 1'b0}), .S2(B), .r(out_3[2:0]));  // open: out_4

  assign out_3[10:3] = A;

  // Other names for the same wires on the sheet: A_t[10:3] = A
endmodule

module CRC_4 (
  input  [3:0] S1,
  input  [3:0] S2,
  output [2:0] r,
  output out_4
);

  wire [3:0] xor_1_out;
  wire [3:3] multiplexer_1_out;

  // Probe on xor_1_out
  assign xor_1_out = S1 ^ S2;  // XOR_Gate xor_1, 4 bits wide
  // Probe on {multiplexer_1_out[3], r}
  Multiplexer #(.width(4)) multiplexer_1 (
    .in0(S1), .in1(xor_1_out), .out({multiplexer_1_out[3], r}), .sel(out_4));  // open: en
  not q (out_4, xor_1_out[3]);
endmodule
