// Logisim project fsm.circ as structural Verilog: 2 circuits, main circuit fsm
module fsm (
  input  CLR,
  input  [1:0] In,
  output out_3
);

  wire clock_1_out, counter_1_q, not_1_out;
  wire [4:0] mealy_1_out_3, multiplexer_1_out, register_1_q;

  mealy mealy_1 (.in_1(multiplexer_1_out), .in_2(In), .out_3(mealy_1_out_3));
  // Probe on mealy_1_out_3
  Clock clock_1 (.out(clock_1_out));
  Register #(.width(5)) register_1 (.D(mealy_1_out_3), .Q(register_1_q), .clk(clock_1_out));  // open: en, clr
  Counter #(.width(1), .max('h1), .ongoal("stay")) counter_1 (
    .Q(counter_1_q), .clk(clock_1_out), .clr(CLR));  // open: load, D, count, carry
  Multiplexer #(.width(5)) multiplexer_1 (
    .in0(5'b00001), .in1(register_1_q), .out(multiplexer_1_out), .sel(counter_1_q));  // open: en
  // Probe on register_1_q
  not not_1 (not_1_out, In[0]);
  and and_1 (out_3, not_1_out, register_1_q[3]);
endmodule

module mealy (
  input  [4:0] in_1,
  input  [1:0] in_2,
  output [4:0] out_3
);

  wire a_c_out, and_1_out, and_2_out, and_3_out, and_4_out, and_5_out, and_6_out, and_7_out, and_8_out,
       and_9_out, and_10_out, decoder_1_out0, decoder_1_out1, decoder_1_out2, decoder_1_out3;

  Decoder #(.select(2)) decoder_1 (
    .out0(decoder_1_out0), .out1(decoder_1_out1), .out2(decoder_1_out2), .out3(decoder_1_out3), .sel(in_2));  // open: en
  or a_c (a_c_out, decoder_1_out0, decoder_1_out2);
  and and_1 (and_1_out, in_1[0], a_c_out);
  and and_2 (and_2_out, in_1[0], decoder_1_out1);
  and and_3 (and_3_out, in_1[1], a_c_out);
  and and_4 (and_4_out, in_1[1], decoder_1_out1);
  and and_5 (and_5_out, in_1[2], a_c_out);
  and and_6 (and_6_out, in_1[2], decoder_1_out1);
  and and_7 (and_7_out, in_1[3], a_c_out);
  and and_8 (and_8_out, in_1[3], decoder_1_out1);
  and and_9 (and_9_out, in_1[4], a_c_out);
  and and_10 (and_10_out, in_1[4], decoder_1_out1);
  or or_1 (out_3[0], decoder_1_out3, and_1_out, and_9_out);
  or or_2 (out_3[1], and_2_out, and_8_out, and_6_out, and_10_out);
  buf or_3 (out_3[2], and_4_out);  // OR_Gate
  or or_4 (out_3[3], and_3_out, and_5_out);
  buf or_5 (out_3[4], and_7_out);  // OR_Gate
endmodule
