// Logisim project ftoi.circ as structural Verilog: 1 circuit, main circuit ftoi
module ftoi (
  input  [15:0] float,
  output [31:0] \int 
);

  wire and_1_out, comparator_1_lt, nor_1_out, or_1_out;
  wire [4:0] subtractor_1_out;
  wire [31:0] ans, multiplexer_1_out, negator_1_out, shifter_1_out, shifter_2_out, shifter_3_out;

  Subtractor #(.width(5)) subtractor_1 (.a(float[14:10]), .b(5'b01111), .out(subtractor_1_out));  // open: bin, bout
  Comparator #(.width(5)) comparator_1 (.a(subtractor_1_out), .b({5{1'b0}}), .lt(comparator_1_lt));  // open: gt, eq
  Shifter #(.width(32)) shifter_1 (.in({22'h1, float[9:0]}), .\dist (subtractor_1_out), .out(shifter_1_out));
  Multiplexer #(.width(32)) multiplexer_1 (
    .in0(shifter_1_out), .in1(shifter_2_out), .out(multiplexer_1_out), .sel(comparator_1_lt));  // open: en
  Shifter #(.width(32), .shift("lr")) shifter_2 (
    .in({22'h1, float[9:0]}), .\dist (subtractor_1_out), .out(shifter_2_out));
  and and_1 (and_1_out, float[10], float[11], float[12], float[13], float[14]);
  nor nor_1 (nor_1_out, float[10], float[11], float[12], float[13], float[14]);
  Shifter #(.width(32), .shift("lr")) shifter_3 (.in(multiplexer_1_out), .\dist (5'b01010), .out(shifter_3_out));
  Multiplexer #(.width(32)) multiplexer_2 (.in0(ans), .in1({32{1'b0}}), .out(\int ), .sel(or_1_out));  // open: en
  or or_1 (or_1_out, and_1_out, nor_1_out);
  Negator #(.width(32)) negator_1 (.in(shifter_3_out), .out(negator_1_out));
  Multiplexer #(.width(32)) multiplexer_3 (
    .in0(shifter_3_out), .in1(negator_1_out), .out(ans), .sel(float[15]));  // open: en

  // Other names for the same wires on the sheet: M[9:0] = float[9:0]; E[4:0] = float[14:10]; S = float[15]
endmodule
