// Logisim project grf.circ as structural Verilog: 2 circuits, main circuit grf
module grf (
  input  clk,
  input  reset,
  input  WE,
  input  [4:0] A1,
  input  [4:0] A2,
  input  [4:0] A3,
  input  [31:0] WD,
  output [31:0] out_8,
  output [31:0] out_9
);

  wire A1_0, A1_1, A1_2, A1_3, A1_4, A1_5, A1_6, A1_7, A1_8, A1_9, A1_10, A1_11, A1_12, A1_13, A1_14, A1_15,
       A1_16, A1_17, A1_18, A1_19, A1_20, A1_21, A1_22, A1_23, A1_24, A1_25, A1_26, A1_27, A1_28, A1_29,
       A1_30, A1_31, A2_0, A2_1, A2_2, A2_3, A2_4, A2_5, A2_6, A2_7, A2_8, A2_9, A2_10, A2_11, A2_12, A2_13,
       A2_14, A2_15, A2_16, A2_17, A2_18, A2_19, A2_20, A2_21, A2_22, A2_23, A2_24, A2_25, A2_26, A2_27,
       A2_28, A2_29, A2_30, A2_31, decoder_3_out0, undriven, W1_1, W1_2, W1_3, W1_4, W1_5, W1_6, W1_7, W1_8,
       W1_9, W1_10, W1_11, W1_12, W1_13, W1_14, W1_15, W1_16, W1_17, W1_18, W1_19, W1_20, W1_21, W1_22,
       W1_23, W1_24, W1_25, W1_26, W1_27, W1_28, W1_29, W1_30, W1_31;
  wire [4:0] multiplexer_1_out;

  Decoder #(.select(5)) decoder_1 (
    .out0(A1_0), .out1(A1_1), .out2(A1_2), .out3(A1_3), .out4(A1_4), .out5(A1_5), .out6(A1_6), .out7(A1_7),
    .out8(A1_8), .out9(A1_9), .out10(A1_10), .out11(A1_11), .out12(A1_12), .out13(A1_13), .out14(A1_14),
    .out15(A1_15), .out16(A1_16), .out17(A1_17), .out18(A1_18), .out19(A1_19), .out20(A1_20), .out21(A1_21),
    .out22(A1_22), .out23(A1_23), .out24(A1_24), .out25(A1_25), .out26(A1_26), .out27(A1_27), .out28(A1_28),
    .out29(A1_29), .out30(A1_30), .out31(A1_31), .sel(A1));  // open: en
  grf_1 grf_1_1 (.A1(A1_0), .A2(A2_0), .RST(reset), .WE(undriven), .clk(clk), .O1(out_8), .O2(out_9));  // open: WD
  grf_1 grf_1_2 (.A1(A1_8), .A2(A2_8), .WD(WD), .RST(reset), .WE(W1_8), .clk(clk), .O1(out_8), .O2(out_9));
  grf_1 grf_1_3 (.A1(A1_16), .A2(A2_16), .WD(WD), .RST(reset), .WE(W1_16), .clk(clk), .O1(out_8), .O2(out_9));
  grf_1 grf_1_4 (.A1(A1_24), .A2(A2_24), .WD(WD), .RST(reset), .WE(W1_24), .clk(clk), .O1(out_8), .O2(out_9));
  grf_1 grf_1_5 (.A1(A1_1), .A2(A2_1), .WD(WD), .RST(reset), .WE(W1_1), .clk(clk), .O1(out_8), .O2(out_9));
  grf_1 grf_1_6 (.A1(A1_9), .A2(A2_9), .WD(WD), .RST(reset), .WE(W1_9), .clk(clk), .O1(out_8), .O2(out_9));
  grf_1 grf_1_7 (.A1(A1_17), .A2(A2_17), .WD(WD), .RST(reset), .WE(W1_17), .clk(clk), .O1(out_8), .O2(out_9));
  grf_1 grf_1_8 (.A1(A1_25), .A2(A2_25), .WD(WD), .RST(reset), .WE(W1_25), .clk(clk), .O1(out_8), .O2(out_9));
  Decoder #(.select(5)) decoder_2 (
    .out0(A2_0), .out1(A2_1), .out2(A2_2), .out3(A2_3), .out4(A2_4), .out5(A2_5), .out6(A2_6), .out7(A2_7),
    .out8(A2_8), .out9(A2_9), .out10(A2_10), .out11(A2_11), .out12(A2_12), .out13(A2_13), .out14(A2_14),
    .out15(A2_15), .out16(A2_16), .out17(A2_17), .out18(A2_18), .out19(A2_19), .out20(A2_20), .out21(A2_21),
    .out22(A2_22), .out23(A2_23), .out24(A2_24), .out25(A2_25), .out26(A2_26), .out27(A2_27), .out28(A2_28),
    .out29(A2_29), .out30(A2_30), .out31(A2_31), .sel(A2));  // open: en
  grf_1 grf_1_9 (.A1(A1_2), .A2(A2_2), .WD(WD), .RST(reset), .WE(W1_2), .clk(clk), .O1(out_8), .O2(out_9));
  grf_1 grf_1_10 (.A1(A1_10), .A2(A2_10), .WD(WD), .RST(reset), .WE(W1_10), .clk(clk), .O1(out_8), .O2(out_9));
  grf_1 grf_1_11 (.A1(A1_18), .A2(A2_18), .WD(WD), .RST(reset), .WE(W1_18), .clk(clk), .O1(out_8), .O2(out_9));
  grf_1 grf_1_12 (.A1(A1_26), .A2(A2_26), .WD(WD), .RST(reset), .WE(W1_26), .clk(clk), .O1(out_8), .O2(out_9));
  grf_1 grf_1_13 (.A1(A1_3), .A2(A2_3), .WD(WD), .RST(reset), .WE(W1_3), .clk(clk), .O1(out_8), .O2(out_9));
  grf_1 grf_1_14 (.A1(A1_11), .A2(A2_11), .WD(WD), .RST(reset), .WE(W1_11), .clk(clk), .O1(out_8), .O2(out_9));
  grf_1 grf_1_15 (.A1(A1_19), .A2(A2_19), .WD(WD), .RST(reset), .WE(W1_19), .clk(clk), .O1(out_8), .O2(out_9));
  grf_1 grf_1_16 (.A1(A1_27), .A2(A2_27), .WD(WD), .RST(reset), .WE(W1_27), .clk(clk), .O1(out_8), .O2(out_9));
  grf_1 grf_1_17 (.A1(A1_4), .A2(A2_4), .WD(WD), .RST(reset), .WE(W1_4), .clk(clk), .O1(out_8), .O2(out_9));
  grf_1 grf_1_18 (.A1(A1_12), .A2(A2_12), .WD(WD), .RST(reset), .WE(W1_12), .clk(clk), .O1(out_8), .O2(out_9));
  grf_1 grf_1_19 (.A1(A1_20), .A2(A2_20), .WD(WD), .RST(reset), .WE(W1_20), .clk(clk), .O1(out_8), .O2(out_9));
  grf_1 grf_1_20 (.A1(A1_28), .A2(A2_28), .WD(WD), .RST(reset), .WE(W1_28), .clk(clk), .O1(out_8), .O2(out_9));
  Decoder #(.select(5)) decoder_3 (
    .out0(decoder_3_out0), .out1(W1_1), .out2(W1_2), .out3(W1_3), .out4(W1_4), .out5(W1_5), .out6(W1_6),
    .out7(W1_7), .out8(W1_8), .out9(W1_9), .out10(W1_10), .out11(W1_11), .out12(W1_12), .out13(W1_13),
    .out14(W1_14), .out15(W1_15), .out16(W1_16), .out17(W1_17), .out18(W1_18), .out19(W1_19), .out20(W1_20),
    .out21(W1_21), .out22(W1_22), .out23(W1_23), .out24(W1_24), .out25(W1_25), .out26(W1_26), .out27(W1_27),
    .out28(W1_28), .out29(W1_29), .out30(W1_30), .out31(W1_31), .sel(multiplexer_1_out));  // open: en
  Multiplexer #(.width(5)) multiplexer_1 (.in0({5{1'b0}}), .in1(A3), .out(multiplexer_1_out), .sel(WE));  // open: en
  grf_1 grf_1_21 (.A1(A1_5), .A2(A2_5), .WD(WD), .RST(reset), .WE(W1_5), .clk(clk), .O1(out_8), .O2(out_9));
  grf_1 grf_1_22 (.A1(A1_13), .A2(A2_13), .WD(WD), .RST(reset), .WE(W1_13), .clk(clk), .O1(out_8), .O2(out_9));
  grf_1 grf_1_23 (.A1(A1_21), .A2(A2_21), .WD(WD), .RST(reset), .WE(W1_21), .clk(clk), .O1(out_8), .O2(out_9));
  grf_1 grf_1_24 (.A1(A1_29), .A2(A2_29), .WD(WD), .RST(reset), .WE(W1_29), .clk(clk), .O1(out_8), .O2(out_9));
  grf_1 grf_1_25 (.A1(A1_6), .A2(A2_6), .WD(WD), .RST(reset), .WE(W1_6), .clk(clk), .O1(out_8), .O2(out_9));
  grf_1 grf_1_26 (.A1(A1_14), .A2(A2_14), .WD(WD), .RST(reset), .WE(W1_14), .clk(clk), .O1(out_8), .O2(out_9));
  grf_1 grf_1_27 (.A1(A1_22), .A2(A2_22), .WD(WD), .RST(reset), .WE(W1_22), .clk(clk), .O1(out_8), .O2(out_9));
  grf_1 grf_1_28 (.A1(A1_30), .A2(A2_30), .WD(WD), .RST(reset), .WE(W1_30), .clk(clk), .O1(out_8), .O2(out_9));
  grf_1 grf_1_29 (.A1(A1_7), .A2(A2_7), .WD(WD), .RST(reset), .WE(W1_7), .clk(clk), .O1(out_8), .O2(out_9));
  grf_1 grf_1_30 (.A1(A1_15), .A2(A2_15), .WD(WD), .RST(reset), .WE(W1_15), .clk(clk), .O1(out_8), .O2(out_9));
  grf_1 grf_1_31 (.A1(A1_23), .A2(A2_23), .WD(WD), .RST(reset), .WE(W1_23), .clk(clk), .O1(out_8), .O2(out_9));
  grf_1 grf_1_32 (.A1(A1_31), .A2(A2_31), .WD(WD), .RST(reset), .WE(W1_31), .clk(clk), .O1(out_8), .O2(out_9));

  // Other names for the same wires on the sheet: RD1[31:0] = out_8; RD2[31:0] = out_9; rst = reset
endmodule

module grf_1 (
  input  RST,
  input  WE,
  input  A1,
  input  A2,
  input  [31:0] WD,
  input  clk,
  output [31:0] O1,
  output [31:0] O2
);

  wire [31:0] register_1_q;

  Register #(.width(32)) register_1 (.D(WD), .en(WE), .Q(register_1_q), .clk(clk), .clr(RST));
  Multiplexer #(.width(32)) multiplexer_1 (.in1(register_1_q), .out(O1), .sel(A1));  // open: in0, en
  Multiplexer #(.width(32)) multiplexer_2 (.in1(register_1_q), .out(O2), .sel(A2));  // open: in0, en
endmodule
