// Logisim project navigation.circ as structural Verilog: 2 circuits, main circuit navigation
module navigation (
  input  [1:0] dir,
  input  clk,
  input  reset,
  output arrive,
  output hit
);

  wire clock_1_out, counter_1_q, logic_1_out_4;
  wire [3:0] multiplexer_2_out;
  wire [4:0] cur_q, logic_1_out_3, multiplexer_1_out;

  Clock clock_1 (.out(clock_1_out));
  // Probe on {arrive, multiplexer_2_out}
  // Probe on logic_1_out_3
  \logic  logic_1 (.cur({arrive, multiplexer_2_out}), .dir(dir), .out_3(logic_1_out_3), .out_4(logic_1_out_4));
  Multiplexer #(.width(5)) multiplexer_1 (
    .in0(logic_1_out_3), .in1(5'b00001), .out(multiplexer_1_out), .sel(arrive));  // open: en
  Register #(.width(5)) cur (.D(multiplexer_1_out), .Q(cur_q), .clk(clock_1_out), .clr(reset));  // open: en
  Register #(.width(1)) u_hit (.D(logic_1_out_4), .Q(hit), .clk(clock_1_out), .clr(reset));  // open: en
  Counter #(.width(1), .max('h1), .ongoal("stay")) counter_1 (
    .Q(counter_1_q), .clk(clock_1_out), .clr(reset));  // open: load, D, count, carry
  Multiplexer #(.width(5)) multiplexer_2 (
    .in0(5'b00001), .in1(cur_q), .out({arrive, multiplexer_2_out}), .sel(counter_1_q));  // open: en
endmodule

module \logic  (
  input  [4:0] cur,
  input  [1:0] dir,
  output [4:0] out_3,
  output out_4
);

  wire and_1_out, and_2_out, and_3_out, and_4_out, and_5_out, and_6_out, and_7_out, and_8_out, and_9_out,
       and_10_out, and_11_out, and_12_out, and_13_out, and_14_out, and_15_out, and_16_out, and_17_out,
       and_18_out, and_19_out, and_20_out, decoder_1_out0, decoder_1_out1, decoder_1_out2, decoder_1_out3;

  Decoder #(.select(2)) decoder_1 (
    .out0(decoder_1_out0), .out1(decoder_1_out1), .out2(decoder_1_out2), .out3(decoder_1_out3), .sel(dir));  // open: en
  and and_1 (and_1_out, cur[0], decoder_1_out0);
  and and_2 (and_2_out, cur[0], decoder_1_out1);
  and and_3 (and_3_out, cur[0], decoder_1_out2);
  and and_4 (and_4_out, cur[0], decoder_1_out3);
  and and_5 (and_5_out, cur[1], decoder_1_out0);
  and and_6 (and_6_out, cur[1], decoder_1_out1);
  and and_7 (and_7_out, cur[1], decoder_1_out2);
  and and_8 (and_8_out, cur[1], decoder_1_out3);
  and and_9 (and_9_out, cur[2], decoder_1_out0);
  and and_10 (and_10_out, cur[2], decoder_1_out1);
  and and_11 (and_11_out, cur[2], decoder_1_out2);
  and and_12 (and_12_out, cur[2], decoder_1_out3);
  and and_13 (and_13_out, cur[3], decoder_1_out0);
  and and_14 (and_14_out, cur[3], decoder_1_out1);
  and and_15 (and_15_out, cur[3], decoder_1_out2);
  and and_16 (and_16_out, cur[3], decoder_1_out3);
  and and_17 (and_17_out, cur[4], decoder_1_out0);
  and and_18 (and_18_out, cur[4], decoder_1_out1);
  and and_19 (and_19_out, cur[4], decoder_1_out2);
  and and_20 (and_20_out, cur[4], cur[2]);
  or or_1 (out_3[0], and_2_out, and_3_out, and_7_out, and_4_out);
  or or_2 (out_3[1], and_8_out, and_1_out, and_12_out, and_15_out);
  or or_3 (out_3[2], and_10_out, and_19_out, and_11_out, and_6_out);
  or or_4 (out_3[3], and_20_out, and_5_out, and_16_out, and_13_out);
  or or_5 (out_3[4], and_17_out, and_9_out, and_18_out, and_14_out);
  or or_6 (out_4, and_13_out, and_16_out, and_2_out, and_3_out, and_4_out, and_8_out, and_10_out, and_11_out);
endmodule
