// Logisim project 4bit_sort.circ as structural Verilog
module _1bit_swap (
  input  A,
  input  B,
  input  S,
  output O1,
  output O2
);

  wire and_1_out, and_2_out, and_3_out, and_4_out, not_1_out, not_2_out;

  not not_1 (not_1_out, S);
  not not_2 (not_2_out, S);
  and and_1 (and_1_out, A, not_1_out);
  or or_1 (O1, and_1_out, and_2_out);
  and and_2 (and_2_out, S, B);
  and and_3 (and_3_out, A, S);
  and and_4 (and_4_out, not_2_out, B);
  or or_2 (O2, and_3_out, and_4_out);
endmodule

module _4bit_swap (
  input  [3:0] input_1,
  input  [3:0] input_2,
  input  selector,
  output [3:0] O1,
  output [3:0] O2
);

  _1bit_swap u_1bit_swap_1 (.A(input_1[0]), .B(input_2[0]), .S(selector), .O1(O1[0]), .O2(O2[0]));
  _1bit_swap u_1bit_swap_2 (.A(input_1[1]), .B(input_2[1]), .S(selector), .O1(O1[1]), .O2(O2[1]));
  _1bit_swap u_1bit_swap_3 (.A(input_1[2]), .B(input_2[2]), .S(selector), .O1(O1[2]), .O2(O2[2]));
  _1bit_swap u_1bit_swap_4 (.A(input_1[3]), .B(input_2[3]), .S(selector), .O1(O1[3]), .O2(O2[3]));

  // Other names for the same wires on the sheet: l1[3:0] = input_1; l2[3:0] = input_2; S = selector
endmodule

module _4bit_sort (
  input  [3:0] A,
  input  [3:0] B,
  input  [3:0] C,
  input  [3:0] D,
  output [3:0] _1,
  output [3:0] _2,
  output [3:0] _3,
  output [3:0] _4
);

  wire comparator_1_gt, comparator_2_gt, comparator_3_gt, comparator_4_gt, comparator_5_gt;
  wire [3:0] A1, B1, B2, C1, D1, D2;

  _4bit_swap u_4bit_swap_1 (.input_1(A), .input_2(B), .selector(comparator_1_gt), .O1(A1), .O2(B1));
  Comparator #(.width(4), .mode("unsigned")) comparator_1 (.a(A), .b(B), .gt(comparator_1_gt));  // open: eq, lt
  _4bit_swap u_4bit_swap_2 (.input_1(C), .input_2(D), .selector(comparator_2_gt), .O1(C1), .O2(D1));
  Comparator #(.width(4), .mode("unsigned")) comparator_2 (.a(C), .b(D), .gt(comparator_2_gt));  // open: eq, lt
  Comparator #(.width(4), .mode("unsigned")) comparator_3 (.a(A1), .b(C1), .gt(comparator_3_gt));  // open: eq, lt
  Comparator #(.width(4), .mode("unsigned")) comparator_4 (.a(B2), .b(D2), .gt(comparator_4_gt));  // open: eq, lt
  Comparator #(.width(4), .mode("unsigned")) comparator_5 (.a(B1), .b(D1), .gt(comparator_5_gt));  // open: eq, lt
  _4bit_swap u_4bit_swap_3 (.input_1(A1), .input_2(C1), .selector(comparator_3_gt), .O1(_1), .O2(B2));
  _4bit_swap u_4bit_swap_4 (.input_1(B2), .input_2(D2), .selector(comparator_4_gt), .O1(_2), .O2(_3));
  _4bit_swap u_4bit_swap_5 (.input_1(B1), .input_2(D1), .selector(comparator_5_gt), .O1(D2), .O2(_4));
endmodule
