// Logisim project fib.circ as structural Verilog: 1 circuit, main circuit main
module main (
  input  [2:0] N,
  output [3:0] Nth
);

  wire and_1_out, clock_1_out, clock_2_out, clock_3_out, cond, counter_1_q, counter_3_q, not_1_out;
  wire [2:0] counter_2_q;
  wire [3:0] adder_1_out, ans, fn_1_q, multiplexer_1_out, multiplexer_2_out, or_1_out, or_2_out;

  Counter #(.width(1), .max('h1), .ongoal("stay")) counter_1 (
    .Q(counter_1_q), .clk(clock_1_out));  // open: load, D, count, carry, clr
  Clock clock_1 (.out(clock_1_out));
  Counter #(.width(3), .max('h7), .ongoal("stay")) counter_2 (
    .Q(counter_2_q), .clk(clock_2_out));  // open: load, D, count, carry, clr
  Clock clock_2 (.out(clock_2_out));
  assign or_1_out = fn_1_q | multiplexer_1_out;  // OR_Gate or_1, 4 bits wide
  Multiplexer #(.width(4)) multiplexer_1 (
    .in0(4'b0001), .in1(4'b0000), .out(multiplexer_1_out), .sel(counter_1_q));  // open: en
  and and_1 (and_1_out, cond, clock_3_out);
  Clock clock_3 (.out(clock_3_out));
  Comparator #(.width(3), .mode("unsigned")) comparator_1 (.a(N), .b(counter_2_q), .gt(cond));  // open: eq, lt
  Register #(.width(4)) fn (.D(or_1_out), .Q(ans), .clk(and_1_out));  // open: en, clr
  Counter #(.width(1), .max('h1), .ongoal("stay")) counter_3 (
    .Q(counter_3_q), .clk(clock_1_out));  // open: load, D, count, carry, clr
  assign or_2_out = adder_1_out | multiplexer_2_out;  // OR_Gate or_2, 4 bits wide
  Multiplexer #(.width(4)) multiplexer_2 (
    .in0(4'b0001), .in1(4'b0000), .out(multiplexer_2_out), .sel(counter_3_q));  // open: en
  Register #(.width(4)) fn_1 (.D(or_2_out), .Q(fn_1_q), .clk(and_1_out));  // open: en, clr
  Multiplexer #(.width(4)) multiplexer_3 (.in0(4'b0000), .in1(ans), .out(Nth), .sel(not_1_out));  // open: en
  not not_1 (not_1_out, cond);
  Adder #(.width(4)) adder_1 (.a(ans), .b(fn_1_q), .out(adder_1_out));  // open: cin, cout
endmodule
