// Logisim project fib_int32.circ as structural Verilog: 2 circuits, main circuit main
module main (
  input  [31:0] in_1,
  output [31:0] Nth
);

  wire clock_1_out, clock_2_out, clock_3_out, clock_4_out, clock_5_out, clock_6_out, clock_7_out,
       clock_8_out, clock_9_out, clock_10_out, clock_11_out, clock_12_out, clock_13_out, clock_14_out,
       clock_15_out, clock_16_out, clock_17_out, clock_18_out, clock_19_out, comparator_2_eq, cond, cond1,
       counter_1_q, counter_2_q, counter_3_q, counter_4_q, counter_5_q, counter_6_q, counter_7_q,
       counter_8_q, counter_9_q, counter_10_q, multiplexer_6_out;
  wire [31:0] and_1_out, ans11, ans12, ans21, ans22, base11, base12, base21, base22, mul_1_out_5,
       mul_2_out_5, mul_3_out_5, mul_4_out_5, mul_5_out_5, mul_6_out_5, mul_7_out_5, mul_8_out_5,
       multiplexer_1_out, multiplexer_2_out, multiplexer_3_out, multiplexer_4_out, multiplexer_5_out,
       multiplexer_7_out, multiplexer_8_out, multiplexer_9_out, multiplexer_10_out, multiplexer_12_out,
       multiplexer_13_out, multiplexer_14_out, multiplexer_15_out, multiplexer_16_out, multiplexer_17_out,
       multiplexer_18_out, multiplexer_19_out, N, or_1_out, or_2_out, or_3_out, or_4_out, or_5_out, or_7_out,
       or_8_out, or_9_out, or_10_out, shifter_1_out;

  Clock clock_1 (.out(clock_1_out));
  Clock clock_2 (.out(clock_2_out));
  Clock clock_3 (.out(clock_3_out));
  Counter #(.width(1), .max('h1), .ongoal("stay")) counter_1 (
    .Q(counter_1_q), .clk(clock_1_out));  // open: load, D, count, carry, clr
  mul mul_1 (.in_1(ans11), .in_2(ans12), .in_3(base11), .in_4(base21), .out_5(mul_1_out_5));
  Multiplexer #(.width(32)) multiplexer_1 (
    .in0(32'h1), .in1({32{1'b0}}), .out(multiplexer_1_out), .sel(counter_2_q));  // open: en
  Counter #(.width(1), .max('h1), .ongoal("stay")) counter_2 (
    .Q(counter_2_q), .clk(clock_2_out));  // open: load, D, count, carry, clr
  mul mul_2 (.in_1(ans21), .in_2(ans22), .in_3(base11), .in_4(base21), .out_5(mul_2_out_5));
  Multiplexer #(.width(32)) multiplexer_2 (
    .in0({32{1'b0}}), .in1({32{1'b0}}), .out(multiplexer_2_out), .sel(counter_3_q));  // open: en
  Counter #(.width(1), .max('h1), .ongoal("stay")) counter_3 (
    .Q(counter_3_q), .clk(clock_3_out));  // open: load, D, count, carry, clr
  Multiplexer #(.width(32)) multiplexer_3 (
    .in0(in_1), .in1({32{1'b0}}), .out(multiplexer_3_out), .sel(counter_1_q));  // open: en
  assign or_1_out = mul_1_out_5 | multiplexer_1_out;  // OR_Gate or_1, 32 bits wide
  assign or_2_out = mul_2_out_5 | multiplexer_2_out;  // OR_Gate or_2, 32 bits wide
  Register #(.width(32)) u_N (.D(or_3_out), .Q(N), .clk(clock_4_out));  // open: en, clr
  assign or_3_out = shifter_1_out | multiplexer_3_out;  // OR_Gate or_3, 32 bits wide
  Clock clock_4 (.out(clock_4_out));
  Multiplexer #(.width(32)) multiplexer_4 (
    .in0(ans11), .in1(or_1_out), .out(multiplexer_4_out), .sel(cond));  // open: en
  Register #(.width(32)) register_1 (.D(multiplexer_4_out), .Q(ans11), .clk(clock_5_out));  // open: en, clr
  Clock clock_5 (.out(clock_5_out));
  Multiplexer #(.width(32)) multiplexer_5 (
    .in0(ans21), .in1(or_2_out), .out(multiplexer_5_out), .sel(cond));  // open: en
  Register #(.width(32)) register_2 (.D(multiplexer_5_out), .Q(ans21), .clk(clock_6_out));  // open: en, clr
  Clock clock_6 (.out(clock_6_out));
  Shifter #(.width(32), .shift("lr")) shifter_1 (.in(N), .\dist (5'b00001), .out(shifter_1_out));
  Counter #(.width(1), .max('h1), .ongoal("stay")) counter_4 (
    .Q(counter_4_q), .clk(clock_7_out));  // open: load, D, count, carry, clr
  Clock clock_7 (.out(clock_7_out));
  Counter #(.width(1), .max('h1), .ongoal("stay")) counter_5 (
    .Q(counter_5_q), .clk(clock_8_out));  // open: load, D, count, carry, clr
  Clock clock_8 (.out(clock_8_out));
  Counter #(.width(1), .max('h1), .ongoal("stay")) counter_6 (
    .Q(counter_6_q), .clk(clock_9_out));  // open: load, D, count, carry, clr
  Clock clock_9 (.out(clock_9_out));
  assign and_1_out = N & 32'h1;  // AND_Gate and_1, 32 bits wide
  Multiplexer multiplexer_6 (.in0(1'b1), .in1(1'b0), .out(multiplexer_6_out), .sel(counter_4_q));  // open: en
  assign or_4_out = mul_3_out_5 | multiplexer_7_out;  // OR_Gate or_4, 32 bits wide
  mul mul_3 (.in_1(ans11), .in_2(ans12), .in_3(base12), .in_4(base22), .out_5(mul_3_out_5));
  Multiplexer #(.width(32)) multiplexer_7 (
    .in0({32{1'b0}}), .in1({32{1'b0}}), .out(multiplexer_7_out), .sel(counter_5_q));  // open: en
  mul mul_4 (.in_1(ans21), .in_2(ans22), .in_3(base12), .in_4(base22), .out_5(mul_4_out_5));
  assign or_5_out = mul_4_out_5 | multiplexer_8_out;  // OR_Gate or_5, 32 bits wide
  Multiplexer #(.width(32)) multiplexer_8 (
    .in0(32'h1), .in1({32{1'b0}}), .out(multiplexer_8_out), .sel(counter_6_q));  // open: en
  Comparator #(.width(32), .mode("unsigned")) comparator_1 (.a(and_1_out), .b({32{1'b0}}), .gt(cond1));  // open: eq, lt
  or or_6 (cond, multiplexer_6_out, cond1);
  Multiplexer #(.width(32)) multiplexer_9 (
    .in0(ans12), .in1(or_4_out), .out(multiplexer_9_out), .sel(cond));  // open: en
  Clock clock_10 (.out(clock_10_out));
  Multiplexer #(.width(32)) multiplexer_10 (
    .in0(ans22), .in1(or_5_out), .out(multiplexer_10_out), .sel(cond));  // open: en
  Clock clock_11 (.out(clock_11_out));
  Register #(.width(32)) register_3 (.D(multiplexer_9_out), .Q(ans12), .clk(clock_10_out));  // open: en, clr
  Register #(.width(32)) register_4 (.D(multiplexer_10_out), .Q(ans22), .clk(clock_11_out));  // open: en, clr
  Comparator #(.width(32), .mode("unsigned")) comparator_2 (
    .a(N), .b({32{1'b0}}), .eq(comparator_2_eq));  // open: gt, lt
  Multiplexer #(.width(32)) multiplexer_11 (
    .in0({32{1'b0}}), .in1(ans21), .out(Nth), .sel(comparator_2_eq));  // open: en
  Counter #(.width(1), .max('h1), .ongoal("stay")) counter_7 (
    .Q(counter_7_q), .clk(clock_12_out));  // open: load, D, count, carry, clr
  Clock clock_12 (.out(clock_12_out));
  Counter #(.width(1), .max('h1), .ongoal("stay")) counter_8 (
    .Q(counter_8_q), .clk(clock_13_out));  // open: load, D, count, carry, clr
  Clock clock_13 (.out(clock_13_out));
  assign or_7_out = mul_5_out_5 | multiplexer_12_out;  // OR_Gate or_7, 32 bits wide
  mul mul_5 (.in_1(base11), .in_2(base12), .in_3(base11), .in_4(base21), .out_5(mul_5_out_5));
  Multiplexer #(.width(32)) multiplexer_12 (
    .in0(32'h1), .in1({32{1'b0}}), .out(multiplexer_12_out), .sel(counter_7_q));  // open: en
  assign or_8_out = mul_6_out_5 | multiplexer_13_out;  // OR_Gate or_8, 32 bits wide
  mul mul_6 (.in_1(base21), .in_2(base22), .in_3(base11), .in_4(base21), .out_5(mul_6_out_5));
  Multiplexer #(.width(32)) multiplexer_13 (
    .in0(32'h1), .in1({32{1'b0}}), .out(multiplexer_13_out), .sel(counter_8_q));  // open: en
  Multiplexer #(.width(32)) multiplexer_14 (
    .in0(base11), .in1(or_7_out), .out(multiplexer_14_out), .sel(1'b1));  // open: en
  Clock clock_14 (.out(clock_14_out));
  Multiplexer #(.width(32)) multiplexer_15 (
    .in0(base21), .in1(or_8_out), .out(multiplexer_15_out), .sel(1'b1));  // open: en
  Clock clock_15 (.out(clock_15_out));
  Register #(.width(32)) register_5 (.D(multiplexer_14_out), .Q(base11), .clk(clock_14_out));  // open: en, clr
  Register #(.width(32)) register_6 (.D(multiplexer_15_out), .Q(base21), .clk(clock_15_out));  // open: en, clr
  Clock clock_16 (.out(clock_16_out));
  Clock clock_17 (.out(clock_17_out));
  mul mul_7 (.in_1(base11), .in_2(base12), .in_3(base12), .in_4(base22), .out_5(mul_7_out_5));
  Multiplexer #(.width(32)) multiplexer_16 (
    .in0(32'h1), .in1({32{1'b0}}), .out(multiplexer_16_out), .sel(counter_9_q));  // open: en
  Counter #(.width(1), .max('h1), .ongoal("stay")) counter_9 (
    .Q(counter_9_q), .clk(clock_16_out));  // open: load, D, count, carry, clr
  mul mul_8 (.in_1(base21), .in_2(base22), .in_3(base12), .in_4(base22), .out_5(mul_8_out_5));
  Multiplexer #(.width(32)) multiplexer_17 (
    .in0({32{1'b0}}), .in1({32{1'b0}}), .out(multiplexer_17_out), .sel(counter_10_q));  // open: en
  Counter #(.width(1), .max('h1), .ongoal("stay")) counter_10 (
    .Q(counter_10_q), .clk(clock_17_out));  // open: load, D, count, carry, clr
  Multiplexer #(.width(32)) multiplexer_18 (
    .in0(base12), .in1(or_9_out), .out(multiplexer_18_out), .sel(1'b1));  // open: en
  assign or_9_out = mul_7_out_5 | multiplexer_16_out;  // OR_Gate or_9, 32 bits wide
  Multiplexer #(.width(32)) multiplexer_19 (
    .in0(base22), .in1(or_10_out), .out(multiplexer_19_out), .sel(1'b1));  // open: en
  assign or_10_out = mul_8_out_5 | multiplexer_17_out;  // OR_Gate or_10, 32 bits wide
  Register #(.width(32)) register_7 (.D(multiplexer_18_out), .Q(base12), .clk(clock_18_out));  // open: en, clr
  Clock clock_18 (.out(clock_18_out));
  Register #(.width(32)) register_8 (.D(multiplexer_19_out), .Q(base22), .clk(clock_19_out));  // open: en, clr
  Clock clock_19 (.out(clock_19_out));
endmodule

module mul (
  input  [31:0] in_1,
  input  [31:0] in_2,
  input  [31:0] in_3,
  input  [31:0] in_4,
  output [31:0] out_5
);

  wire [31:0] multiplier_1_out, multiplier_2_out;

  Multiplier #(.width(32)) multiplier_1 (.a(in_1), .b(in_3), .out(multiplier_1_out));  // open: cin, cout
  Multiplier #(.width(32)) multiplier_2 (.a(in_2), .b(in_4), .out(multiplier_2_out));  // open: cin, cout
  Adder #(.width(32)) adder_1 (.a(multiplier_1_out), .b(multiplier_2_out), .out(out_5));  // open: cin, cout
endmodule
