// Logisim project mod5.circ as structural Verilog: 2 circuits, main circuit mod5
module mod5 (
  input  In,
  output S0,
  output S1,
  output S2,
  output S3,
  output S4
);

  wire clock_1_out, counter_1_q;
  wire [3:0] multiplexer_1_out, register_1_q;

  fsm fsm_1 (.in_1(multiplexer_1_out), .in_2(In), .out_3({S4, S3, S2, S1}));
  Register #(.width(4)) register_1 (.D({S4, S3, S2, S1}), .en(1'b1), .Q(register_1_q), .clk(clock_1_out));  // open: clr
  Counter #(.width(1), .max('h1), .ongoal("stay")) counter_1 (
    .Q(counter_1_q), .clk(clock_1_out));  // open: load, D, count, carry, clr
  Clock clock_1 (.out(clock_1_out));
  Multiplexer #(.width(4)) multiplexer_1 (
    .in0(4'b0001), .in1(register_1_q), .out(multiplexer_1_out), .sel(counter_1_q));  // open: en

  assign S0 = 1'b0;
endmodule

module fsm (
  input  [3:0] in_1,
  input  in_2,
  output [3:0] out_3
);

  wire and_1_out, and_2_out, and_3_out, and_4_out, and_5_out, and_6_out, and_7_out, and_8_out, not_1_out;

  not not_1 (not_1_out, in_2);
  and and_1 (and_1_out, not_1_out, in_1[0]);
  and and_2 (and_2_out, in_2, in_1[0]);
  and and_3 (and_3_out, not_1_out, in_1[1]);
  and and_4 (and_4_out, in_2, in_1[1]);
  and and_5 (and_5_out, not_1_out, in_1[2]);
  and and_6 (and_6_out, in_2, in_1[2]);
  and and_7 (and_7_out, not_1_out, in_1[3]);
  and and_8 (and_8_out, in_2, in_1[3]);
  or or_1 (out_3[0], and_1_out, and_7_out);
  or or_2 (out_3[1], and_2_out, and_8_out);
  or or_3 (out_3[2], and_4_out, and_6_out);
  or or_4 (out_3[3], and_5_out, and_3_out);

  // Other names for the same wires on the sheet: in[3:0] = in_1; S = in_2
endmodule
